// Logisim project Trabalho_SD.circ as structural Verilog: 4 circuits, main circuit main
module main (
  input  BI,
  input  SPA,
  input  SRS,
  input  ST,
  output Elemento_de_Aquecimento,
  output Motor_Esquerdo,
  output Motor_Direito
);

  wire \MAQ_módulo_de_controlo_da_temperatura , \MAQ_módulo_de_controlo_do_motor ;

  \Módulo_de_Controlo_da_Máquina  MAQ (
    .BI(BI), .SPA(SPA), .SRS(SRS),
    .\Módulo_de_Controlo_da_Temperatura (\MAQ_módulo_de_controlo_da_temperatura ),
    .\Módulo_de_Controlo_do_Motor (\MAQ_módulo_de_controlo_do_motor ));
  \Módulo_de_Controlo_da_Temperatura  MCT (
    .MAQ(\MAQ_módulo_de_controlo_da_temperatura ), .SPA(SPA), .SRS(SRS), .ST(ST),
    .Elemento_de_Aquecimento(Elemento_de_Aquecimento));
  \Módulo_de_Controlo_do_Motor  MTR (
    .MAQ(\MAQ_módulo_de_controlo_do_motor ), .SPA(SPA), .SRS(SRS), .Motor_Esquerdo(Motor_Esquerdo),
    .Motor_Direito(Motor_Direito));
endmodule

module \Módulo_de_Controlo_da_Máquina  (
  input  BI,
  input  SPA,
  input  SRS,
  output \Módulo_de_Controlo_da_Temperatura ,
  output \Módulo_de_Controlo_do_Motor 
);

  wire and_1_out, and_2_out, and_3_out, and_4_out, clock_1_out, not_1_out, not_2_out, not_3_out, not_4_out,
       not_5_out, or_1_out, t_ff_1_qn;

  Clock clock_1 (.out(clock_1_out));
  not not_1 (not_1_out, SPA);
  not not_2 (not_2_out, SRS);
  not not_3 (not_3_out, not_5_out);
  and and_1 (and_1_out, BI, not_1_out, not_2_out, not_3_out);
  not not_4 (not_4_out, BI);
  and and_2 (and_2_out, not_4_out, not_5_out);
  and and_3 (and_3_out, SPA, not_5_out);
  and and_4 (and_4_out, SRS, not_5_out);
  or or_1 (or_1_out, and_1_out, and_2_out, and_3_out, and_4_out);
  T_Flip_Flop t_ff_1 (
    .clk(clock_1_out), .T(or_1_out), .Q(\Módulo_de_Controlo_da_Temperatura ), .Qn(t_ff_1_qn));  // open: preset, reset, en
  not not_5 (not_5_out, t_ff_1_qn);

  assign \Módulo_de_Controlo_do_Motor  = \Módulo_de_Controlo_da_Temperatura ;
endmodule

module \Módulo_de_Controlo_da_Temperatura  (
  input  MAQ,
  input  SPA,
  input  SRS,
  input  ST,
  output Elemento_de_Aquecimento
);

  wire and_1_out, and_2_out, and_3_out, and_4_out, and_5_out, clock_1_out, not_1_out, not_2_out, not_3_out,
       not_4_out, not_5_out, not_6_out, or_1_out, t_ff_1_qn;

  Clock clock_1 (.out(clock_1_out));
  not not_1 (not_1_out, SPA);
  not not_2 (not_2_out, SRS);
  not not_3 (not_3_out, ST);
  not not_4 (not_4_out, t_ff_1_qn);
  not not_5 (not_5_out, MAQ);
  not not_6 (not_6_out, not_4_out);
  and and_1 (and_1_out, not_5_out, not_4_out);
  and and_2 (and_2_out, MAQ, not_1_out, not_2_out, not_3_out, not_6_out);
  and and_3 (and_3_out, SPA, not_4_out);
  and and_4 (and_4_out, SRS, not_4_out);
  and and_5 (and_5_out, ST, not_4_out);
  or or_1 (or_1_out, and_1_out, and_2_out, and_3_out, and_4_out, and_5_out);
  T_Flip_Flop t_ff_1 (
    .clk(clock_1_out), .T(or_1_out), .Q(Elemento_de_Aquecimento), .Qn(t_ff_1_qn));  // open: preset, reset, en
endmodule

module \Módulo_de_Controlo_do_Motor  (
  input  MAQ,
  input  SPA,
  input  SRS,
  output Motor_Esquerdo,
  output Motor_Direito
);

  wire and_1_out, and_2_out, and_3_out, and_4_out, and_5_out, and_6_out, and_7_out, and_8_out, and_9_out,
       and_10_out, clock_1_out, not_1_out, not_2_out, not_3_out, not_4_out, not_5_out, not_6_out, not_7_out,
       not_8_out, not_9_out, not_10_out, not_11_out, not_12_out, not_13_out, not_14_out, or_1_out, or_2_out,
       or_3_out, T0_q, T0_qn, T1_q, T1_qn, T2_q, T2_qn;

  Clock clock_1 (.out(clock_1_out));
  not not_1 (not_1_out, SPA);
  not not_2 (not_2_out, SRS);
  not not_3 (not_3_out, T0_qn);
  not not_4 (not_4_out, MAQ);
  not not_5 (not_5_out, T1_qn);
  and and_1 (and_1_out, MAQ, not_1_out, not_2_out, not_3_out, not_5_out);
  and and_2 (and_2_out, T2_qn, not_3_out, MAQ, not_2_out, not_1_out);
  and and_3 (and_3_out, not_5_out, not_4_out);
  and and_4 (and_4_out, not_5_out, SRS);
  and and_5 (and_5_out, not_5_out, SPA);
  and and_6 (and_6_out, not_5_out, not_6_out);
  not not_6 (not_6_out, T2_qn);
  and and_7 (and_7_out, T1_qn, MAQ, not_7_out, not_8_out);
  not not_7 (not_7_out, SPA);
  not not_8 (not_8_out, SRS);
  and and_8 (and_8_out, T2_qn, MAQ, not_9_out, not_10_out);
  not not_9 (not_9_out, SPA);
  not not_10 (not_10_out, SRS);
  not not_11 (not_11_out, T0_qn);
  or or_1 (or_1_out, T2_q, and_1_out);
  or or_2 (or_2_out, and_2_out, and_3_out, and_4_out, and_5_out, and_6_out);
  or or_3 (or_3_out, and_7_out, not_11_out, and_8_out);
  T_Flip_Flop T2 (.clk(clock_1_out), .T(or_1_out), .Q(T2_q), .Qn(T2_qn));  // open: preset, reset, en
  T_Flip_Flop T1 (.clk(clock_1_out), .T(or_2_out), .Q(T1_q), .Qn(T1_qn));  // open: preset, reset, en
  T_Flip_Flop T0 (.clk(clock_1_out), .T(or_3_out), .Q(T0_q), .Qn(T0_qn));  // open: preset, reset, en
  not not_12 (not_12_out, T2_q);
  and and_9 (and_9_out, not_12_out, T1_q, T0_q);
  and and_10 (and_10_out, T2_q, not_13_out, not_14_out);
  not not_13 (not_13_out, T1_q);
  not not_14 (not_14_out, T0_q);
  xor xor_1 (Motor_Direito, T1_q, T0_q);
  or or_4 (Motor_Esquerdo, and_9_out, and_10_out);
endmodule
